# Fritzing sketch paeiot-sensor-one (saved by Fritzing 0.9.3b)
circuit board: 1.7911cm x 3.68471cm
breadboards: 1

parts:
  Part2 = Arduino MKR WAN 1310
  AM2 = AM2302 Humidity and Temperature Sensor
  J3 = female pin header, 3 pins [form="♀ (female)"]
  J4 = male pin header, 3 pins [form="♂ (male)"]
  J5 = male pin header, 3 pins [form="♂ (male)"]
  J2 = female pin header, 3 pins [form="♀ (female)"]
  AM1 = AM2302 Humidity and Temperature Sensor

nets:
  N1: Part2.RESET, Part2.D14/TX
  N2: Part2.GND, J3.pin3, J2.pin3
  N3: Part2.D2, J3.pin1
  N4: Part2.D3~, J2.pin1
  N5: Part2.D11/MOSI, Part2.+5V
  N6: Part2.+3V3, J3.pin2, J2.pin2
  N7: AM2.VDD, J4.pin2
  N8: AM2.DATA, J4.pin1
  N9: AM2.GND, J4.pin3
  N10: J5.pin1, AM1.DATA
  N11: J5.pin2, AM1.VDD
  N12: J5.pin3, AM1.GND

custom parts:
  Arduino MKR WAN 1310: The Arduino MKR WAN 1310 board provides a practical and cost effective solution to add LoRa® connectivity to projects requiring low power. This open source board can be connected to: the Arduino IoT Cloud, your own LoRa® network using the Arduino LoRa® PRO Gateway, existing LoRaWAN™ infrastructure like The Things Network, or even other boards using the direct connectivity mode.
